// Digital circuit Lobinho.dig as structural Verilog
module Lobinho (
  input  clk
);

  wire button_1_out, button_2_out, button_3_out, button_4_out, u_PoliLobinho_db_clock;
  wire [6:0] not_1_out, not_2_out, not_3_out, not_4_out, u_PoliLobinho_db_classe_atual,
       u_PoliLobinho_db_estado_7b, u_PoliLobinho_db_jogador_atual, u_PoliLobinho_db_seed_7b;

  Button #(.activeLow("true")) button_1 (.out(button_1_out));
  Button #(.activeLow("true")) button_2 (.out(button_2_out));
  Button #(.activeLow("true")) button_3 (.out(button_3_out));
  Button #(.activeLow("true")) button_4 (.out(button_4_out));
  PoliLobinho #(.applicationType("IVERILOG"), .CodeFile("C:\\Users\\anton\\Documents\\PoliLobinho\\digital.v")) u_PoliLobinho (
    .clock(clk), .botao(button_1_out), .reset(button_2_out), .jogar(button_3_out), .passa(button_4_out),
    .db_classe_atual(u_PoliLobinho_db_classe_atual), .db_jogador_atual(u_PoliLobinho_db_jogador_atual),
    .db_estado_7b(u_PoliLobinho_db_estado_7b), .db_seed_7b(u_PoliLobinho_db_seed_7b),
    .db_clock(u_PoliLobinho_db_clock));
  LED led_1 (.in(u_PoliLobinho_db_clock));
  assign not_1_out = ~u_PoliLobinho_db_classe_atual;  // Not not_1, 7 bits wide
  Seven_Seg seven_seg_1 (
    .a(not_1_out[0]), .b(not_1_out[1]), .c(not_1_out[2]), .d(not_1_out[3]), .e(not_1_out[4]),
    .f(not_1_out[5]), .g(not_1_out[6]), .dp(1'b0));
  assign not_2_out = ~u_PoliLobinho_db_seed_7b;  // Not not_2, 7 bits wide
  Seven_Seg seven_seg_2 (
    .a(not_2_out[0]), .b(not_2_out[1]), .c(not_2_out[2]), .d(not_2_out[3]), .e(not_2_out[4]),
    .f(not_2_out[5]), .g(not_2_out[6]), .dp(1'b0));
  assign not_3_out = ~u_PoliLobinho_db_jogador_atual;  // Not not_3, 7 bits wide
  Seven_Seg seven_seg_3 (
    .a(not_3_out[0]), .b(not_3_out[1]), .c(not_3_out[2]), .d(not_3_out[3]), .e(not_3_out[4]),
    .f(not_3_out[5]), .g(not_3_out[6]), .dp(1'b0));
  assign not_4_out = ~u_PoliLobinho_db_estado_7b;  // Not not_4, 7 bits wide
  Seven_Seg seven_seg_4 (
    .a(not_4_out[0]), .b(not_4_out[1]), .c(not_4_out[2]), .d(not_4_out[3]), .e(not_4_out[4]),
    .f(not_4_out[5]), .g(not_4_out[6]), .dp(1'b0));

  // Notes on the sheet:
  //   clk: Hz: 1000
  //   Classe
  //   Seed
  //   Jogador
  //   Estado
endmodule
